# Fritzing sketch Untitled Sketch 2 (saved by Fritzing 0.9.3b)
breadboards: 1

parts:
  Part1 = Arduino Uno (Rev3) - ICSP
  Part2 = LCD1602-I2C
  M1 = fc-51 [package=THT]
  M2 = fc-51 [package=THT]
  J1 = Basic Servo

nets:
  N1: Part1.A4/SDA, Part2.SDA
  N2: Part1.A5/SCL, Part2.SCL
  N3: Part1.D2, M2.pin1
  N4: Part1.D3_PWM, J1.pulse
  N5: Part1.D4, M1.pin1
  VCC: Part1.5V, Part2.VCC, M1.pin3, M2.pin3, J1.vcc
  GND: Part1.GND, Part2.GND, M1.pin2, M2.pin2, J1.gnd

custom parts:
  LCD1602-I2C: A standard character display, usually with 2x16 characters. Comes in many colors with LCM1602 IIC attached.
